// Logisim project EXP-1.circ as structural Verilog: 1 circuit, main circuit main
module main (
  input  in_1,
  input  in_2,
  input  in_3,
  input  in_4,
  input  in_5,
  output out_6,
  output out_7,
  output out_8,
  output out_9
);

  wire and_2_out, and_3_out, xor_1_out;

  xor xor_1 (xor_1_out, in_1, in_2);
  xor xor_2 (out_8, in_4, in_5);
  and and_1 (out_9, in_4, in_5);
  and and_2 (and_2_out, xor_1_out, in_3);
  and and_3 (and_3_out, in_1, in_2);
  xor xor_3 (out_6, xor_1_out, in_3);
  or or_1 (out_7, and_2_out, and_3_out);

  // Notes on the sheet:
  //   FULL ADDER
  //   HALF ADDER
endmodule
