// Logisim project EXP-2(8X3 Encoder).circ as structural Verilog: 1 circuit, main circuit main
module main (
  input  in_1,
  input  in_2,
  input  in_3,
  input  in_4,
  input  in_5,
  input  in_6,
  input  in_7,
  input  in_8,
  output out_9,
  output out_10,
  output out_11
);

  or or_1 (out_9, in_5, in_6, in_7, in_8);
  or or_2 (out_10, in_3, in_4, in_7, in_8);
  or or_3 (out_11, in_2, in_4, in_6, in_8);

  // Notes on the sheet:
  //   D0
  //   D1
  //   D2
  //   D3
  //   D4
  //   D5
  //   D6
  //   D7
endmodule
