// Logisim project EXP-3(4 bit ripple carry).circ as structural Verilog: 1 circuit, main circuit main
module main (
  input  in_1,
  input  in_2,
  input  in_3,
  input  in_4,
  input  in_5,
  input  in_6,
  input  in_7,
  input  in_8,
  input  in_9,
  output out_10,
  output out_11,
  output out_12,
  output out_13,
  output out_14
);

  wire and_1_out, and_2_out, and_3_out, and_4_out, and_5_out, and_6_out, and_7_out, and_8_out, or_1_out,
       or_2_out, or_3_out, xor_1_out, xor_2_out, xor_3_out, xor_4_out;

  xor xor_1 (xor_1_out, in_2, in_6);
  and and_1 (and_1_out, in_2, in_6);
  xor xor_2 (xor_2_out, in_3, in_7);
  and and_2 (and_2_out, in_3, in_7);
  xor xor_3 (xor_3_out, in_4, in_8);
  and and_3 (and_3_out, in_4, in_8);
  xor xor_4 (xor_4_out, in_5, in_9);
  and and_4 (and_4_out, in_5, in_9);
  xor xor_5 (out_10, xor_1_out, in_1);
  and and_5 (and_5_out, in_1, xor_1_out);
  xor xor_6 (out_11, xor_2_out, or_1_out);
  and and_6 (and_6_out, or_1_out, xor_2_out);
  xor xor_7 (out_12, xor_3_out, or_2_out);
  and and_7 (and_7_out, xor_3_out, or_2_out);
  xor xor_8 (out_13, xor_4_out, or_3_out);
  and and_8 (and_8_out, xor_4_out, or_3_out);
  or or_1 (or_1_out, and_5_out, and_1_out);
  or or_2 (or_2_out, and_6_out, and_2_out);
  or or_3 (or_3_out, and_7_out, and_3_out);
  or or_4 (out_14, and_8_out, and_4_out);

  // Notes on the sheet:
  //   INPUT A
  //   INPUT B
  //   SUM
endmodule
