// Logisim project EXP-6.circ as structural Verilog: 1 circuit, main circuit main
module main (
  input  s1,
  input  s0,
  output out_3,
  output out_4,
  output out_5,
  output out_6
);

  wire undriven_4, undriven_6, undriven_8, undriven_12, undriven_14, undriven_15, undriven_18, undriven_20,
       undriven_22, undriven_25, undriven_27, undriven_29;
  wire [1:1] undriven;
  wire [3:0] undriven_2, undriven_3, undriven_5, undriven_7, undriven_9, undriven_10, undriven_11,
       undriven_13, undriven_16, undriven_17, undriven_19, undriven_21, undriven_23, undriven_24,
       undriven_26, undriven_28;
  wire [3:1] multiplexer_1_out, multiplexer_2_out, multiplexer_3_out, multiplexer_4_out;

  Shift_Register #(.length(4)) shift_register_1 (
    .load(undriven_2[0]), .d0(undriven_4), .d1(undriven_6), .d2(undriven_8));  // open: shift, in, clk, out, clr, q0, q1, q2, d3, q3
  Multiplexer #(.select(2), .width(4), .disabled(0)) multiplexer_1 (
    .in0(undriven_2), .in1(undriven_3), .in2(undriven_5), .in3(undriven_7), .out({multiplexer_1_out, out_3}),
    .sel({undriven[1], s0}), .en(s1));
  Multiplexer #(.select(2), .width(4), .disabled(0)) multiplexer_2 (
    .in0(undriven_9), .in1(undriven_10), .in2(undriven_11), .in3(undriven_13),
    .out({multiplexer_2_out, out_4}), .sel({undriven[1], s0}), .en(s1));
  Shift_Register #(.length(4)) shift_register_2 (
    .load(undriven_3[0]), .d0(undriven_12), .d1(undriven_14), .d2(undriven_15));  // open: shift, in, clk, out, clr, q0, q1, q2, d3, q3
  Multiplexer #(.select(2), .width(4), .disabled(0)) multiplexer_3 (
    .in0(undriven_16), .in1(undriven_17), .in2(undriven_19), .in3(undriven_21),
    .out({multiplexer_3_out, out_5}), .sel({undriven[1], s0}), .en(s1));
  Shift_Register #(.length(4)) shift_register_3 (
    .load(undriven_5[0]), .d0(undriven_18), .d1(undriven_20), .d2(undriven_22));  // open: shift, in, clk, out, clr, q0, q1, q2, d3, q3
  Shift_Register #(.length(4)) shift_register_4 (
    .load(undriven_7[0]), .d0(undriven_25), .d1(undriven_27), .d2(undriven_29));  // open: shift, in, clk, out, clr, q0, q1, q2, d3, q3
  Multiplexer #(.select(2), .width(4), .disabled(0)) multiplexer_4 (
    .in0(undriven_23), .in1(undriven_24), .in2(undriven_26), .in3(undriven_28),
    .out({multiplexer_4_out, out_6}), .sel({undriven[1], s0}), .en(s1));
  // Pins of 1 and 4 bits meet at undriven_7
  // Pins of 1 and 4 bits meet at {multiplexer_2_out, out_4}
  // Pins of 1 and 2 bits meet at {undriven[1], s0}
  // Pins of 1 and 4 bits meet at undriven_2
  // Pins of 1 and 4 bits meet at {multiplexer_3_out, out_5}
  // Pins of 1 and 4 bits meet at undriven_3
  // Pins of 1 and 4 bits meet at undriven_5
  // Pins of 1 and 4 bits meet at {multiplexer_1_out, out_3}
  // Pins of 1 and 4 bits meet at {multiplexer_4_out, out_6}

  // Notes on the sheet:
  //   Reg-D
  //   Reg-C
  //   Reg-B
  //   Reg-A
  //   4-line common bus
endmodule
